# Fritzing sketch SchemaLCD_i2c (saved by Fritzing 0.9.3b)
circuit board: 4.75147cm x 3.17843cm
breadboards: 1

parts:
  U1 = PCF8574 [package="DIP16 [THT]"]
  Q1 = NPN-Transistor [part_number=2N2222 package="TO92 [THT]"]
  Componente1 = Arduino Uno (Rev3)
  R2 = TRIMPOT [package=trimpot_pth_s3_lock_3386P]
  J1 = female pin header, 2 pins [form="♀ (female)"]
  LCD1 = LCD screen
  J2 = female pin header, 2 pins [form="♀ (female)"]

nets (from the breadboard view):
  GND: U1.A0, U1.A1, U1.A3, U1.GND, Q1.C, Componente1.GND, R2.CW, J1.pin2, LCD1.VSS
  N1: U1.P0, LCD1.DB4
  N2: U1.P1, LCD1.DB5
  N3: U1.P2, LCD1.DB6
  N4: U1.P3, LCD1.DB7
  N5: U1.P4, LCD1.E
  N6: U1.P5, LCD1.R/W
  N7: U1.P6, LCD1.RS
  N8: U1.P7, Q1.B
  N9: U1.SCL, Componente1.A5/SCL, J2.pin2
  N10: U1.SDA, Componente1.A4/SDA, J2.pin1
  VCC: U1.VCC, Componente1.5V, R2.CCW, J1.pin1, LCD1.VDD, LCD1.LED+
  N11: Q1.E, LCD1.LED-
  N12: R2.WIPER, LCD1.V0

notes:
  Indirizzo
  Re
  ef
  la-+

custom parts:
  TRIMPOT: Various small potentiometers for set-and-forget applications
