# Fritzing sketch SchemaLCD_i2c_standardv02 (saved by Fritzing 0.9.3b)
circuit board: 4.79182cm x 3.4cm
breadboards: 1

parts:
  Componente1 = Arduino Uno (Rev3)
  J1 = female pin header, 2 pins [form="♀ (female)"]
  U2 = PCF8574 [package="DIP16 [THT]"]
  J2 = female pin header, 2 pins [form="♀ (female)"]
  R3 = TRIMPOT [package=trimpot_pth_s3_lock_3386P]
  Q1 = NPN-Transistor [package="TO92 [THT]"]
  LCD1 = LCD screen

nets:
  N1: Componente1.A4/SDA, U2.SDA, J2.pin1
  N2: Componente1.A5/SCL, U2.SCL, J2.pin2
  5V: Componente1.5V, J1.pin1, U2.VCC, R3.CCW, LCD1.VDD, LCD1.LED+
  GND: Componente1.GND, J1.pin2, U2.A0, U2.A1, U2.A3, U2.GND, R3.CW, Q1.C, LCD1.VSS
  N3: U2.P0, LCD1.RS
  N4: U2.P1, LCD1.R/W
  N5: U2.P2, LCD1.E
  N6: U2.P3, Q1.B
  N7: U2.P4, LCD1.DB4
  N8: U2.P5, LCD1.DB5
  N9: U2.P6, LCD1.DB6
  N10: U2.P7, LCD1.DB7
  N11: R3.WIPER, LCD1.V0
  N12: Q1.E, LCD1.LED-

notes:
  Address
  REEF LCD

custom parts:
  TRIMPOT: Various small potentiometers for set-and-forget applications
