# Fritzing sketch SchemaLCD_i2c_standardv03 (saved by Fritzing 0.9.3b)
circuit board: 4.79182cm x 3.4cm
breadboards: 1

parts:
  Componente1 = Arduino Uno (Rev3)
  J1 = female pin header, 2 pins [form="♀ (female)"]
  J2 = female pin header, 2 pins [form="♀ (female)"]
  R3 = TRIMPOT [package=trimpot_pth_s3_lock_3386P]
  Q1 = NPN-Transistor [package="TO92 [THT]"]
  LCD1 = LCD screen
  IC1 = IC, DIP package, 16 pins [chip_label=IC]

nets:
  N1: Componente1.A4/SDA, J2.pin1, IC1.pin15
  N2: Componente1.A5/SCL, J2.pin2, IC1.pin14
  5V: Componente1.5V, J1.pin1, R3.CCW, LCD1.VDD, LCD1.LED+, IC1.pin16
  GND: Componente1.GND, J1.pin2, R3.CW, Q1.C, LCD1.VSS, IC1.pin1, IC1.pin2, IC1.pin3, IC1.pin8
  N3: R3.WIPER, LCD1.V0
  N4: Q1.E, LCD1.LED-
  N5: Q1.B, IC1.pin7
  N6: LCD1.RS, IC1.pin4
  N7: LCD1.R/W, IC1.pin5
  N8: LCD1.E, IC1.pin6
  N9: LCD1.DB4, IC1.pin9
  N10: LCD1.DB5, IC1.pin10
  N11: LCD1.DB6, IC1.pin11
  N12: LCD1.DB7, IC1.pin12

notes:
  Address
  REEF LCD

custom parts:
  TRIMPOT: Various small potentiometers for set-and-forget applications
